# Fritzing sketch arduino_uno_pn532_i2c (saved by Fritzing 1.0.6)

parts:
  Composant1 = Arduino Uno (Rev3) - ICSP
  Composant2 = PN532 Elechouse RFID NFC Module V3

nets:
  N1: Composant1.A4/SDA, Composant2.SDA
  N2: Composant1.A5/SCL, Composant2.SCL
  N3: Composant1.D2, Composant2.IRQ
  N4: Composant1.D3_PWM, Composant2.RSTO
  5V: Composant1.5V, Composant2.VCC
  GND: Composant1.GND, Composant2.GND

custom parts:
  PN532 Elechouse RFID NFC Module V3: NFC is a popular technology in recent years. We often heard this work while smart phone company such as Samsung or HTC introduces their latest high-end phones. Almost all the high-end phone in the market support NFC. Near field communication (NFC) is a set of standards for smart phones and similar devices to establish radio communication with each other by touching them together or bringing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
